// Logisim project p3_CPU.circ as structural Verilog: 9 circuits, main circuit main
module main (
  input  in_1,
  output [31:0] Instr,
  output [31:0] pc,
  output RegWrite,
  output [4:0] RegAddr,
  output [31:0] RegData,
  output MemWrite,
  output [31:0] MemAddr,
  output [31:0] MemData
);

  wire ALUsrc, Branch, clk, equal, jump, MemtoReg, MUDIOp, RegDst;
  wire [1:0] EXTOp;
  wire [2:0] ALUOp;
  wire [4:0] _0, base, rd, rs, rt;
  wire [5:0] func, opcode;
  wire [15:0] splitter_1_offset_imm;
  wire [25:0] jump_addr;
  wire [31:0] dm_1_out_7, hiData, loData, multiplexer_2_out, off_imm, rsData;

  Clock clock_1 (.out(clk));
  GRF grf_1 (
    .RD2(rsData), .RD1(MemData), .WD(RegData), .WE(RegWrite), .clk(clk), .reset(in_1), .A3(RegAddr), .A2(rs),
    .A1(rt));
  Controller controller_1 (
    .opcode(opcode), .func(func), .out_3(RegWrite), .out_4(RegDst), .out_5(ALUsrc), .out_6(Branch),
    .out_7(MemWrite), .out_8(MemtoReg), .out_11(EXTOp), .out_12(ALUOp), .out_9(jump), .out_10(MUDIOp));
  IFU ifu_1 (
    .clk(clk), .reset(in_1), .Branch(Branch), .equal(equal), .imm(off_imm), .PC(pc), .Instr(Instr),
    .jump_addr(jump_addr), .jump(jump));
  Splitter splitter_1 (
    .Instr(Instr), .opcode(opcode), .rs(rs), .rt(rt), .rd(rd), ._0(_0), .func(func),
    .offset_imm(splitter_1_offset_imm), .base(base), .instr_index(jump_addr));
  // Probe on Instr
  Multiplexer #(.width(5), .enable("false")) multiplexer_1 (.in0(rt), .in1(rd), .out(RegAddr), .sel(RegDst));
  EXT ext_1 (.in_1(splitter_1_offset_imm), .EXTOp(EXTOp), .out_3(off_imm));
  ALU alu_1 (.A(rsData), .B(multiplexer_2_out), .out_4(MemAddr), .zero(equal), .ALUOp(ALUOp));  // open: greater, less
  Multiplexer #(.width(32), .enable("false")) multiplexer_2 (
    .in0(MemData), .in1(off_imm), .out(multiplexer_2_out), .sel(ALUsrc));
  DM dm_1 (.Addr(MemAddr), .Data(MemData), .WE(MemWrite), .clk(clk), .RE(1'b1), .reset(in_1), .out_7(dm_1_out_7));
  Multiplexer #(.width(32), .enable("false")) multiplexer_3 (
    .in0(MemAddr), .in1(dm_1_out_7), .out(RegData), .sel(MemtoReg));
  MUDI mudi_1 (.A(rsData), .B(MemData), .in_3(MUDIOp), .in_4(1'b1), .in_5(clk), .in_6(in_1), .lo(loData), .hi(hiData));

  // Other names for the same wires on the sheet: ALURes[31:0] = MemAddr; reset = in_1; rtData[31:0] = MemData

  // Notes on the sheet:
  //   GRF
  //   Splitter
  //   Controller
  //   Controller
  //   IFU
  //   EXT
  //   ALU
  //   DM
endmodule

module GRF (
  input  reset,
  input  clk,
  input  WE,
  input  [31:0] WD,
  input  [4:0] A3,
  input  [4:0] A2,
  input  [4:0] A1,
  output [31:0] RD2,
  output [31:0] RD1
);

  wire I00, I01, I02, I03, I04, I05, I06, I07, I08, I09, I10, I11, I12, I13, I14, I15, I16, I17, I18, I19,
       I20, I21, I22, I23, I24, I25, I26, I27, I28, I29, I30, I31;
  wire [31:0] multiplexer_1_out, multiplexer_2_out, multiplexer_3_out, multiplexer_4_out, multiplexer_5_out,
       multiplexer_6_out, multiplexer_7_out, multiplexer_8_out, multiplexer_9_out, multiplexer_10_out,
       multiplexer_11_out, multiplexer_12_out, multiplexer_13_out, multiplexer_14_out, multiplexer_15_out,
       multiplexer_16_out, multiplexer_17_out, multiplexer_18_out, multiplexer_19_out, multiplexer_20_out,
       multiplexer_21_out, multiplexer_22_out, multiplexer_23_out, multiplexer_24_out, multiplexer_25_out,
       multiplexer_26_out, multiplexer_27_out, multiplexer_28_out, multiplexer_29_out, multiplexer_30_out,
       multiplexer_31_out, multiplexer_32_out, O00, O01, O02, O03, O04, O05, O06, O07, O08, O09, O10, O11,
       O12, O13, O14, O15, O16, O17, O18, O19, O20, O21, O22, O23, O24, O25, O26, O27, O28, O29, O30, O31;

  Multiplexer #(.width(32), .enable("false")) multiplexer_1 (.in0(O00), .in1(WD), .out(multiplexer_1_out), .sel(I00));
  Multiplexer #(.width(32), .enable("false")) multiplexer_2 (.in0(O04), .in1(WD), .out(multiplexer_2_out), .sel(I04));
  Multiplexer #(.width(32), .enable("false")) multiplexer_3 (.in0(O08), .in1(WD), .out(multiplexer_3_out), .sel(I08));
  Multiplexer #(.width(32), .enable("false")) multiplexer_4 (.in0(O12), .in1(WD), .out(multiplexer_4_out), .sel(I12));
  Multiplexer #(.width(32), .enable("false")) multiplexer_5 (.in0(O16), .in1(WD), .out(multiplexer_5_out), .sel(I16));
  Multiplexer #(.width(32), .enable("false")) multiplexer_6 (.in0(O20), .in1(WD), .out(multiplexer_6_out), .sel(I20));
  Multiplexer #(.width(32), .enable("false")) multiplexer_7 (.in0(O24), .in1(WD), .out(multiplexer_7_out), .sel(I24));
  Multiplexer #(.width(32), .enable("false")) multiplexer_8 (.in0(O28), .in1(WD), .out(multiplexer_8_out), .sel(I28));
  Register #(.width(32)) R00 (.D(multiplexer_1_out), .en(WE), .Q(O00), .clk(clk), .clr(1'b1));
  Register #(.width(32)) R04 (.D(multiplexer_2_out), .en(WE), .Q(O04), .clk(clk), .clr(reset));
  Register #(.width(32)) R08 (.D(multiplexer_3_out), .en(WE), .Q(O08), .clk(clk), .clr(reset));
  Register #(.width(32)) R12 (.D(multiplexer_4_out), .en(WE), .Q(O12), .clk(clk), .clr(reset));
  Register #(.width(32)) R16 (.D(multiplexer_5_out), .en(WE), .Q(O16), .clk(clk), .clr(reset));
  Register #(.width(32)) R20 (.D(multiplexer_6_out), .en(WE), .Q(O20), .clk(clk), .clr(reset));
  Register #(.width(32)) R24 (.D(multiplexer_7_out), .en(WE), .Q(O24), .clk(clk), .clr(reset));
  Register #(.width(32)) R28 (.D(multiplexer_8_out), .en(WE), .Q(O28), .clk(clk), .clr(reset));
  Multiplexer #(.width(32), .enable("false")) multiplexer_9 (.in0(O01), .in1(WD), .out(multiplexer_9_out), .sel(I01));
  Multiplexer #(.width(32), .enable("false")) multiplexer_10 (.in0(O05), .in1(WD), .out(multiplexer_10_out), .sel(I05));
  Multiplexer #(.width(32), .enable("false")) multiplexer_11 (.in0(O09), .in1(WD), .out(multiplexer_11_out), .sel(I09));
  Multiplexer #(.width(32), .enable("false")) multiplexer_12 (.in0(O13), .in1(WD), .out(multiplexer_12_out), .sel(I13));
  Multiplexer #(.width(32), .enable("false")) multiplexer_13 (.in0(O17), .in1(WD), .out(multiplexer_13_out), .sel(I17));
  Multiplexer #(.width(32), .enable("false")) multiplexer_14 (.in0(O21), .in1(WD), .out(multiplexer_14_out), .sel(I21));
  Multiplexer #(.width(32), .enable("false")) multiplexer_15 (.in0(O25), .in1(WD), .out(multiplexer_15_out), .sel(I25));
  Multiplexer #(.width(32), .enable("false")) multiplexer_16 (.in0(O29), .in1(WD), .out(multiplexer_16_out), .sel(I29));
  Register #(.width(32)) R01 (.D(multiplexer_9_out), .en(WE), .Q(O01), .clk(clk), .clr(reset));
  Register #(.width(32)) R05 (.D(multiplexer_10_out), .en(WE), .Q(O05), .clk(clk), .clr(reset));
  Register #(.width(32)) R09 (.D(multiplexer_11_out), .en(WE), .Q(O09), .clk(clk), .clr(reset));
  Register #(.width(32)) R13 (.D(multiplexer_12_out), .en(WE), .Q(O13), .clk(clk), .clr(reset));
  Register #(.width(32)) R17 (.D(multiplexer_13_out), .en(WE), .Q(O17), .clk(clk), .clr(reset));
  Register #(.width(32)) R21 (.D(multiplexer_14_out), .en(WE), .Q(O21), .clk(clk), .clr(reset));
  Register #(.width(32)) R25 (.D(multiplexer_15_out), .en(WE), .Q(O25), .clk(clk), .clr(reset));
  Register #(.width(32)) R29 (.D(multiplexer_16_out), .en(WE), .Q(O29), .clk(clk), .clr(reset));
  Multiplexer #(.width(32), .enable("false")) multiplexer_17 (.in0(O02), .in1(WD), .out(multiplexer_17_out), .sel(I02));
  Register #(.width(32)) R02 (.D(multiplexer_17_out), .en(WE), .Q(O02), .clk(clk), .clr(reset));
  Multiplexer #(.width(32), .enable("false")) multiplexer_18 (.in0(O06), .in1(WD), .out(multiplexer_18_out), .sel(I06));
  Register #(.width(32)) R06 (.D(multiplexer_18_out), .en(WE), .Q(O06), .clk(clk), .clr(reset));
  Register #(.width(32)) R10 (.D(multiplexer_19_out), .en(WE), .Q(O10), .clk(clk), .clr(reset));
  Multiplexer #(.width(32), .enable("false")) multiplexer_19 (.in0(O10), .in1(WD), .out(multiplexer_19_out), .sel(I10));
  Multiplexer #(.width(32), .enable("false")) multiplexer_20 (.in0(O14), .in1(WD), .out(multiplexer_20_out), .sel(I14));
  Register #(.width(32)) R14 (.D(multiplexer_20_out), .en(WE), .Q(O14), .clk(clk), .clr(reset));
  Register #(.width(32)) R18 (.D(multiplexer_21_out), .en(WE), .Q(O18), .clk(clk), .clr(reset));
  Multiplexer #(.width(32), .enable("false")) multiplexer_21 (.in0(O18), .in1(WD), .out(multiplexer_21_out), .sel(I18));
  Multiplexer #(.width(32), .enable("false")) multiplexer_22 (.in0(O22), .in1(WD), .out(multiplexer_22_out), .sel(I22));
  Register #(.width(32)) R22 (.D(multiplexer_22_out), .en(WE), .Q(O22), .clk(clk), .clr(reset));
  Multiplexer #(.width(32), .enable("false")) multiplexer_23 (.in0(O26), .in1(WD), .out(multiplexer_23_out), .sel(I26));
  Register #(.width(32)) R26 (.D(multiplexer_23_out), .en(WE), .Q(O26), .clk(clk), .clr(reset));
  Register #(.width(32)) R30 (.D(multiplexer_24_out), .en(WE), .Q(O30), .clk(clk), .clr(reset));
  Multiplexer #(.width(32), .enable("false")) multiplexer_24 (.in0(O30), .in1(WD), .out(multiplexer_24_out), .sel(I30));
  Multiplexer #(.width(32), .enable("false")) multiplexer_25 (.in0(O03), .in1(WD), .out(multiplexer_25_out), .sel(I03));
  Multiplexer #(.width(32), .enable("false")) multiplexer_26 (.in0(O07), .in1(WD), .out(multiplexer_26_out), .sel(I07));
  Multiplexer #(.width(32), .enable("false")) multiplexer_27 (.in0(O11), .in1(WD), .out(multiplexer_27_out), .sel(I11));
  Multiplexer #(.width(32), .enable("false")) multiplexer_28 (.in0(O15), .in1(WD), .out(multiplexer_28_out), .sel(I15));
  Multiplexer #(.width(32), .enable("false")) multiplexer_29 (.in0(O19), .in1(WD), .out(multiplexer_29_out), .sel(I19));
  Multiplexer #(.width(32), .enable("false")) multiplexer_30 (.in0(O23), .in1(WD), .out(multiplexer_30_out), .sel(I23));
  Multiplexer #(.width(32), .enable("false")) multiplexer_31 (.in0(O27), .in1(WD), .out(multiplexer_31_out), .sel(I27));
  Multiplexer #(.width(32), .enable("false")) multiplexer_32 (.in0(O31), .in1(WD), .out(multiplexer_32_out), .sel(I31));
  Register #(.width(32)) R03 (.D(multiplexer_25_out), .en(WE), .Q(O03), .clk(clk), .clr(reset));
  Register #(.width(32)) R07 (.D(multiplexer_26_out), .en(WE), .Q(O07), .clk(clk), .clr(reset));
  Register #(.width(32)) R11 (.D(multiplexer_27_out), .en(WE), .Q(O11), .clk(clk), .clr(reset));
  Register #(.width(32)) R15 (.D(multiplexer_28_out), .en(WE), .Q(O15), .clk(clk), .clr(reset));
  Register #(.width(32)) R19 (.D(multiplexer_29_out), .en(WE), .Q(O19), .clk(clk), .clr(reset));
  Register #(.width(32)) R23 (.D(multiplexer_30_out), .en(WE), .Q(O23), .clk(clk), .clr(reset));
  Register #(.width(32)) R27 (.D(multiplexer_31_out), .en(WE), .Q(O27), .clk(clk), .clr(reset));
  Register #(.width(32)) R31 (.D(multiplexer_32_out), .en(WE), .Q(O31), .clk(clk), .clr(reset));
  Decoder #(.select(5), .enable("false")) decoder_1 (
    .out0(I00), .out1(I01), .out2(I02), .out3(I03), .out4(I04), .out5(I05), .out6(I06), .out7(I07),
    .out8(I08), .out9(I09), .out10(I10), .out11(I11), .out12(I12), .out13(I13), .out14(I14), .out15(I15),
    .out16(I16), .out17(I17), .out18(I18), .out19(I19), .out20(I20), .out21(I21), .out22(I22), .out23(I23),
    .out24(I24), .out25(I25), .out26(I26), .out27(I27), .out28(I28), .out29(I29), .out30(I30), .out31(I31),
    .sel(A3));
  Multiplexer #(.select(5), .width(32), .enable("false")) multiplexer_33 (
    .in0(O00), .in1(O01), .in2(O02), .in3(O03), .in4(O04), .in5(O05), .in6(O06), .in7(O07), .in8(O08),
    .in9(O09), .in10(O10), .in11(O11), .in12(O12), .in13(O13), .in14(O14), .in15(O15), .in16(O16),
    .in17(O17), .in18(O18), .in19(O19), .in20(O20), .in21(O21), .in22(O22), .in23(O23), .in24(O24),
    .in25(O25), .in26(O26), .in27(O27), .in28(O28), .in29(O29), .in30(O30), .in31(O31), .out(RD2), .sel(A2));
  Multiplexer #(.select(5), .width(32), .enable("false")) multiplexer_34 (
    .in0(O00), .in1(O01), .in2(O02), .in3(O03), .in4(O04), .in5(O05), .in6(O06), .in7(O07), .in8(O08),
    .in9(O09), .in10(O10), .in11(O11), .in12(O12), .in13(O13), .in14(O14), .in15(O15), .in16(O16),
    .in17(O17), .in18(O18), .in19(O19), .in20(O20), .in21(O21), .in22(O22), .in23(O23), .in24(O24),
    .in25(O25), .in26(O26), .in27(O27), .in28(O28), .in29(O29), .in30(O30), .in31(O31), .out(RD1), .sel(A1));
endmodule

module Controller (
  input  [5:0] opcode,
  input  [5:0] func,
  output out_3,
  output out_4,
  output out_5,
  output out_6,
  output out_7,
  output out_8,
  output out_9,
  output out_10,
  output [1:0] out_11,
  output [2:0] out_12
);

  wire add, beq, div, j, lui, lw, mult, not_1_out, not_2_out, not_3_out, not_4_out, not_5_out, not_6_out,
       not_7_out, not_8_out, not_9_out, not_10_out, not_11_out, not_12_out, op_000000, ori, sll, sub, sw;

  or RegWrite (out_3, ori, lw, mult, div, lui, add, sub);
  or RegDst (out_4, add, sub);
  not not_1 (not_1_out, opcode[5]);
  not not_2 (not_2_out, opcode[4]);
  or ALUsrc (out_5, ori, lw, sw, lui);
  not not_3 (not_3_out, opcode[3]);
  not not_4 (not_4_out, opcode[2]);
  buf Branch (out_6, beq);  // OR_Gate
  not not_5 (not_5_out, opcode[1]);
  not not_6 (not_6_out, opcode[0]);
  buf MemWrite (out_7, sw);  // OR_Gate
  buf MemtoReg (out_8, lw);  // OR_Gate
  and _000000 (op_000000, not_6_out, not_5_out, not_4_out, not_3_out, not_2_out, not_1_out);
  and u_ori (ori, opcode[0], not_5_out, opcode[2], opcode[3], not_2_out, not_1_out);
  and u_lw (lw, opcode[0], opcode[1], not_4_out, not_3_out, not_2_out, opcode[5]);
  and u_sw (sw, opcode[0], opcode[1], not_4_out, opcode[3], not_2_out, opcode[5]);
  and u_beq (beq, not_6_out, not_5_out, opcode[2], not_3_out, not_2_out, not_1_out);
  and u_lui (lui, opcode[0], opcode[1], opcode[2], opcode[3], not_2_out, not_1_out);
  and u_add (add, op_000000, func[5], not_7_out, not_10_out, not_9_out, not_11_out, not_12_out);
  and u_sub (sub, op_000000, func[5], not_7_out, not_10_out, not_9_out, func[1], not_12_out);
  and u_j (j, not_6_out, opcode[1], not_4_out, not_3_out, not_2_out, not_1_out);
  and u_mult (mult, op_000000, not_8_out, func[4], func[3], not_9_out, not_11_out, not_12_out);
  and u_div (div, op_000000, not_8_out, func[4], func[3], not_9_out, func[1], func[0]);
  and u_sll (sll, op_000000, not_8_out, not_7_out, not_10_out, not_9_out, not_11_out, not_12_out);
  buf EXTOp1 (out_11[1], lui);  // OR_Gate
  or EXTOp0 (out_11[0], lw, sw, beq);
  not not_7 (not_7_out, func[4]);
  not not_8 (not_8_out, func[5]);
  buf ALUOp2 (out_12[2], sll);  // OR_Gate
  not not_9 (not_9_out, func[2]);
  not not_10 (not_10_out, func[3]);
  not not_11 (not_11_out, func[1]);
  not not_12 (not_12_out, func[0]);
  or ALUOp1 (out_12[1], ori, lui);
  or ALUOp0 (out_12[0], beq, sub);
  buf jump (out_9, j);  // OR_Gate
  buf MUDIOp (out_10, div);  // OR_Gate

  // Other names for the same wires on the sheet: f0 = func[0]; f1 = func[1]; f2 = func[2]; f3 = func[3]; f4 = func[4];
  //   f5 = func[5]; op0 = opcode[0]; op1 = opcode[1]; op2 = opcode[2]; op3 = opcode[3]; op4 = opcode[4];
  //   op5 = opcode[5]
endmodule

module ALU (
  input  [31:0] A,
  input  [2:0] ALUOp,
  input  [31:0] B,
  output [31:0] out_4,
  output greater,
  output zero,
  output less
);

  wire [31:0] add, \and , \or , sll, sub;

  Adder #(.width(32)) adder_1 (.a(A), .b(B), .out(add));  // open: cin, cout
  Subtractor #(.width(32)) subtractor_1 (.a(A), .b(B), .out(sub));  // open: bin, bout
  assign \or  = A | B;  // OR_Gate or_1, 32 bits wide
  assign \and  = A & B;  // AND_Gate and_1, 32 bits wide
  Shifter #(.width(32)) shifter_1 (.in(A), .\dist (B[4:0]), .out(sll));
  Multiplexer #(.select(3), .width(32), .enable("false")) multiplexer_1 (
    .in0(add), .in1(sub), .in2(\or ), .in3(\and ), .in4(sll), .out(out_4), .sel(ALUOp));  // open: in5, in6, in7
  Comparator #(.width(32)) comparator_1 (.a(out_4), .b({32{1'b0}}), .gt(greater), .eq(zero), .lt(less));
endmodule

module EXT (
  input  [15:0] in_1,
  input  [1:0] EXTOp,
  output [31:0] out_3
);

  wire [31:0] bit_extender_1_out, bit_extender_2_out, bit_extender_3_out, shifter_1_out;

  assign bit_extender_1_out = {{16{1'b0}}, in_1};  // Bit_Extender bit_extender_1
  assign bit_extender_2_out = {{16{in_1[15]}}, in_1};  // Bit_Extender bit_extender_2
  assign bit_extender_3_out = {{16{1'b0}}, in_1};  // Bit_Extender bit_extender_3
  Shifter #(.width(32)) shifter_1 (.in(bit_extender_3_out), .\dist (5'b10000), .out(shifter_1_out));
  Multiplexer #(.select(2), .width(32), .enable("false")) multiplexer_1 (
    .in0(bit_extender_1_out), .in1(bit_extender_2_out), .in2(shifter_1_out), .out(out_3), .sel(EXTOp));  // open: in3
endmodule

module Splitter (
  input  [31:0] Instr,
  output [5:0] opcode,
  output [4:0] rs,
  output [4:0] rt,
  output [4:0] rd,
  output [4:0] _0,
  output [5:0] func,
  output [15:0] offset_imm,
  output [4:0] base,
  output [25:0] instr_index
);


  assign _0 = Instr[10:6];
  assign base = Instr[25:21];
  assign func = Instr[5:0];
  assign instr_index = Instr[25:0];
  assign offset_imm = Instr[15:0];
  assign opcode = Instr[31:26];
  assign rd = Instr[15:11];
  assign rs = Instr[25:21];
  assign rt = Instr[20:16];
endmodule

module IFU (
  input  clk,
  input  reset,
  input  Branch,
  input  equal,
  input  [31:0] imm,
  input  [25:0] jump_addr,
  input  jump,
  output [31:0] PC,
  output [31:0] Instr
);

  wire beq, comparator_1_eq;
  wire [3:0] adder_1_out_2;
  wire [27:0] adder_1_out, bit_extender_1_out, shifter_1_out;
  wire [31:0] adder_2_out, multiplexer_1_out, multiplexer_2_out, register_1_q, shifter_2_out,
       subtractor_1_out;

  assign bit_extender_1_out = {{2{1'b0}}, jump_addr};  // Bit_Extender bit_extender_1
  Shifter #(.width(28)) shifter_1 (.in(bit_extender_1_out), .\dist (5'b00010), .out(shifter_1_out));
  and and_1 (beq, Branch, equal);
  Adder #(.width(32)) adder_1 (.a(PC), .b(32'h4), .out({adder_1_out_2, adder_1_out}));  // open: cin, cout
  Adder #(.width(32)) adder_2 (
    .a({adder_1_out_2, adder_1_out}), .b(shifter_2_out), .out(adder_2_out));  // open: cin, cout
  Shifter #(.width(32)) shifter_2 (.in(imm), .\dist (5'b00010), .out(shifter_2_out));
  Multiplexer #(.width(32), .enable("false")) multiplexer_1 (
    .in0({adder_1_out_2, adder_1_out}), .in1(adder_2_out), .out(multiplexer_1_out), .sel(beq));
  Register #(.width(32)) register_1 (.D(multiplexer_2_out), .Q(register_1_q), .clk(clk), .clr(reset));  // open: en
  Multiplexer #(.width(32), .enable("false")) multiplexer_2 (
    .in0(multiplexer_1_out), .in1({adder_1_out_2, shifter_1_out}), .out(multiplexer_2_out), .sel(jump));
  Comparator #(.width(32), .mode("unsigned")) comparator_1 (
    .a(register_1_q), .b({32{1'b0}}), .eq(comparator_1_eq));  // open: gt, lt
  Multiplexer #(.width(32), .enable("false")) multiplexer_3 (
    .in0(register_1_q), .in1(32'h3000), .out(PC), .sel(comparator_1_eq));
  Subtractor #(.width(32)) subtractor_1 (.a(PC), .b(32'h3000), .out(subtractor_1_out));  // open: bin, bout
  ROM #(.addrWidth(12), .dataWidth(32)) rom_1 (.addr(subtractor_1_out[13:2]), .data(Instr));  // open: sel

  // Notes on the sheet:
  //   contents of rom_1 (hex, n*v repeats v):
  //   3c081234 35085678 3c090001 3529ffff 340a00ff 340b0000 340c0005 340d000a 3c0effff 35cefff0 3c0fffff
  //   35effff8 16c8020 18d8820 1cf9020 12a9820 10aa020 18d0020 16ca822 1aeb022 12ab822 14a5822 1ac0022
  //   afb1fffc 8fa9fffc afb6fff8 8faafff8 afb5fff4 8facfff4 afb7fff0 8fa0fff0 120c0001 0 12290001 0
  //   10000001 0 340e000a 34180001 1d87022 11cb0003 0 1000fffb
endmodule

module DM (
  input  [31:0] Addr,
  input  [31:0] Data,
  input  WE,
  input  clk,
  input  RE,
  input  reset,
  output [31:0] out_7
);

  RAM #(.addrWidth(12), .dataWidth(32), .bus("separate")) ram_1 (
    .addr(Addr[13:2]), .din(Data), .data(out_7), .str(WE), .clk(clk), .ld(RE), .clr(reset));  // open: sel
endmodule

module MUDI (
  input  [31:0] A,
  input  [31:0] B,
  input  in_3,
  input  in_4,
  input  in_5,
  input  in_6,
  output [31:0] lo,
  output [31:0] hi
);

  wire [31:0] divhi, divlo, multhi, multiplexer_1_out, multiplexer_2_out, multlo;

  Multiplier #(.width(32)) multiplier_1 (.a(A), .b(B), .out(multlo), .cout(multhi));  // open: cin
  Divider #(.width(32)) divider_1 (.a(A), .b(B), .out(divlo), .rem(divhi));  // open: upper
  Multiplexer #(.width(32), .enable("false")) multiplexer_1 (
    .in0(multlo), .in1(divlo), .out(multiplexer_1_out), .sel(in_3));
  Multiplexer #(.width(32), .enable("false")) multiplexer_2 (
    .in0(multhi), .in1(divhi), .out(multiplexer_2_out), .sel(in_3));
  Register #(.width(32)) register_1 (.D(multiplexer_1_out), .en(in_4), .Q(lo), .clk(in_5), .clr(in_6));
  Register #(.width(32)) register_2 (.D(multiplexer_2_out), .en(in_4), .Q(hi), .clk(in_5), .clr(in_6));

  // Other names for the same wires on the sheet: clk = in_5; MUDIOp = in_3; reset = in_6; WE = in_4
endmodule
